// Logisim project cpu.circ as structural Verilog: 21 circuits, main circuit main
module main (
  input  reset
);

  wire alu_1_equivalent, alu_1_gore, clk, IM, inn, jalWE, keyboard_1_avail, memory_latch_1_oe_latched,
       memory_latch_1_we_latched, multiplexer_4_out, RAMwe, RDwe, RWD, RWE, TTYwe;
  wire [1:0] b, PCop;
  wire [2:0] ALUop, multiplexer_2_out, rd, rs, rt, sa;
  wire [3:0] instructionsplitter_1_opcode;
  wire [5:0] instructionsplitter_1_immed;
  wire [6:0] bit_extender_3_out, keyboard_1_data;
  wire [7:7] not_1_out;
  wire [11:0] addr;
  wire [15:0] alu_1_outputdata, DW, Imm, InReg, memory_latch_1_address_latched,
       memory_latch_1_data_in_latched, multiplexer_1_out, multiplexer_3_out, multiplexer_5_out, nxt, PC,
       pcnav_1_norm, ram_1_dout, registerfile_1_reg2readdata, rom_1_data, rsVal;

  PC pc_1 (.out_4(PC), .rst(reset), .in_1(nxt), .clk(clk));
  Clock clock_1 (.out(clk));
  ROM #(.addrWidth(16), .dataWidth(16)) rom_1 (.addr(PC), .data(rom_1_data));
  OpCrl opcrl_1 (
    .TTY(TTYwe), .RDwe(RDwe), .AddImm(IM), .RAMwe(RAMwe), .RWE(RWE), .ALUop(ALUop),
    .OpCode(instructionsplitter_1_opcode), .InputWE(inn), .jalWE(jalWE), .RWD(RWD), .b(b), .PCop(PCop));
  InstructionSplitter instructionsplitter_1 (
    .shamt(sa), .opcode(instructionsplitter_1_opcode), .adrs(addr), .rt(rt), .rs(rs), .rd(rd),
    .Ins(rom_1_data), .Immed(instructionsplitter_1_immed));
  Keyboard keyboard_1 (.clk(clk), .re(inn), .clr(reset), .avail(keyboard_1_avail), .data(keyboard_1_data));
  not not_1 (not_1_out[7], keyboard_1_avail);
  assign Imm = {{10{instructionsplitter_1_immed[5]}}, instructionsplitter_1_immed};  // Bit_Extender bit_extender_1
  assign InReg = {{8{1'b0}}, {not_1_out[7], keyboard_1_data}};  // Bit_Extender bit_extender_2
  Multiplexer #(.width(16), .enable("false")) multiplexer_1 (.in0(DW), .in1(InReg), .out(multiplexer_1_out), .sel(inn));
  Bit_Extender #(.in_width(16), .out_width(7), .\type ("zero")) bit_extender_3 (.in(rsVal), .out(bit_extender_3_out));
  TTY #(.rows(13), .cols(80)) tty_1 (.data(bit_extender_3_out), .clk(clk), .we(TTYwe), .clr(reset));
  RegisterFile registerfile_1 (
    .Register1(rs), .Reg1ReadData(rsVal), .reset(reset), .Data(multiplexer_1_out), .Register2(rt), .WE(RWE),
    .Reg2ReadData(registerfile_1_reg2readdata), .Clock(clk), .PickWE(multiplexer_2_out), .jalWE(jalWE));
  Multiplexer #(.width(3), .enable("false")) multiplexer_2 (.in0(rt), .in1(rd), .out(multiplexer_2_out), .sel(RDwe));
  Multiplexer #(.width(16), .enable("false")) multiplexer_3 (
    .in0(registerfile_1_reg2readdata), .in1(Imm), .out(multiplexer_3_out), .sel(IM));
  Multiplexer #(.select(2), .enable("false")) multiplexer_4 (
    .in1(alu_1_equivalent), .in2(alu_1_gore), .out(multiplexer_4_out), .sel(b));  // open: in0, in3
  PCNav pcnav_1 (
    .addr(addr), .rs(rsVal), .Imm(Imm), .PC(PC), .PCop(PCop), .nxt(nxt), .b(multiplexer_4_out),
    .norm(pcnav_1_norm));
  ALU alu_1 (
    .Shamt(sa), .InputData2(multiplexer_3_out), .equivalent(alu_1_equivalent), .ALUop(ALUop),
    .GorE(alu_1_gore), .InputData1(rsVal), .OutputData(alu_1_outputdata));
  memory_latch memory_latch_1 (
    .OE_latched(memory_latch_1_oe_latched), .WE_latched(memory_latch_1_we_latched),
    .address_latched(memory_latch_1_address_latched), .data_in(registerfile_1_reg2readdata), .clk(clk),
    .WE(RAMwe), .address(alu_1_outputdata), .data_in_latched(memory_latch_1_data_in_latched));
  RAM #(.addrWidth(16), .dataWidth(16), .trigger("high"), .databus("bibus")) ram_1 (
    .addr(memory_latch_1_address_latched), .we(memory_latch_1_we_latched), .oe(memory_latch_1_oe_latched),
    .din(memory_latch_1_data_in_latched), .dout(ram_1_dout));
  Multiplexer #(.width(16), .enable("false")) multiplexer_5 (
    .in0(alu_1_outputdata), .in1(ram_1_dout), .out(multiplexer_5_out), .sel(RWD));
  Multiplexer #(.width(16), .enable("false")) multiplexer_6 (
    .in0(multiplexer_5_out), .in1(pcnav_1_norm), .out(DW), .sel(jalWE));
endmodule

module Register16 (
  input  [15:0] In16Bits,
  input  reset,
  input  we,
  input  clock,
  output [15:0] Out16Bits
);

  wire clk;

  and and_1 (clk, we, clock);
  D_Flip_Flop d_ff_1 (.D(In16Bits[0]), .clk(clk), .Q(Out16Bits[0]), .reset(reset));  // open: Qn, preset
  D_Flip_Flop d_ff_2 (.D(In16Bits[4]), .clk(clk), .Q(Out16Bits[4]), .reset(reset));  // open: Qn, preset
  D_Flip_Flop d_ff_3 (.D(In16Bits[8]), .clk(clk), .Q(Out16Bits[8]), .reset(reset));  // open: Qn, preset
  D_Flip_Flop d_ff_4 (.D(In16Bits[12]), .clk(clk), .Q(Out16Bits[12]), .reset(reset));  // open: Qn, preset
  D_Flip_Flop d_ff_5 (.D(In16Bits[1]), .clk(clk), .Q(Out16Bits[1]), .reset(reset));  // open: Qn, preset
  D_Flip_Flop d_ff_6 (.D(In16Bits[5]), .clk(clk), .Q(Out16Bits[5]), .reset(reset));  // open: Qn, preset
  D_Flip_Flop d_ff_7 (.D(In16Bits[9]), .clk(clk), .Q(Out16Bits[9]), .reset(reset));  // open: Qn, preset
  D_Flip_Flop d_ff_8 (.D(In16Bits[13]), .clk(clk), .Q(Out16Bits[13]), .reset(reset));  // open: Qn, preset
  D_Flip_Flop d_ff_9 (.D(In16Bits[2]), .clk(clk), .Q(Out16Bits[2]), .reset(reset));  // open: Qn, preset
  D_Flip_Flop d_ff_10 (.D(In16Bits[6]), .clk(clk), .Q(Out16Bits[6]), .reset(reset));  // open: Qn, preset
  D_Flip_Flop d_ff_11 (.D(In16Bits[10]), .clk(clk), .Q(Out16Bits[10]), .reset(reset));  // open: Qn, preset
  D_Flip_Flop d_ff_12 (.D(In16Bits[14]), .clk(clk), .Q(Out16Bits[14]), .reset(reset));  // open: Qn, preset
  D_Flip_Flop d_ff_13 (.D(In16Bits[3]), .clk(clk), .Q(Out16Bits[3]), .reset(reset));  // open: Qn, preset
  D_Flip_Flop d_ff_14 (.D(In16Bits[7]), .clk(clk), .Q(Out16Bits[7]), .reset(reset));  // open: Qn, preset
  D_Flip_Flop d_ff_15 (.D(In16Bits[11]), .clk(clk), .Q(Out16Bits[11]), .reset(reset));  // open: Qn, preset
  D_Flip_Flop d_ff_16 (.D(In16Bits[15]), .clk(clk), .Q(Out16Bits[15]), .reset(reset));  // open: Qn, preset

  // Other names for the same wires on the sheet: i0 = In16Bits[0]; i1 = In16Bits[1]; i2 = In16Bits[2];
  //   i3 = In16Bits[3]; i4 = In16Bits[4]; i5 = In16Bits[5]; i6 = In16Bits[6]; i7 = In16Bits[7]; i8 = In16Bits[8];
  //   i9 = In16Bits[9]; i10 = In16Bits[10]; i11 = In16Bits[11]; i12 = In16Bits[12]; i13 = In16Bits[13];
  //   i14 = In16Bits[14]; i15 = In16Bits[15]; o0 = Out16Bits[0]; o1 = Out16Bits[1]; o2 = Out16Bits[2];
  //   o3 = Out16Bits[3]; o4 = Out16Bits[4]; o5 = Out16Bits[5]; o6 = Out16Bits[6]; o7 = Out16Bits[7];
  //   o8 = Out16Bits[8]; o9 = Out16Bits[9]; o10 = Out16Bits[10]; o11 = Out16Bits[11]; o12 = Out16Bits[12];
  //   o13 = Out16Bits[13]; o14 = Out16Bits[14]; o15 = Out16Bits[15]; rst = reset
endmodule

module RegisterFile (
  input  WE,
  input  Clock,
  input  reset,
  input  [2:0] Register1,
  input  [2:0] Register2,
  input  [2:0] PickWE,
  input  jalWE,
  input  [15:0] Data,
  output [15:0] Reg1ReadData,
  output [15:0] Reg2ReadData
);

  wire Re1sel0, Re1sel1, Re1sel2, Re1sel3, Re1sel4, Re1sel5, Re1sel6, Re1sel7, Re2sel0, Re2sel1, Re2sel2,
       Re2sel3, Re2sel4, Re2sel5, Re2sel6, Re2sel7, we0, we1, we2, we3, we4, we5, we6, we7;
  wire [2:0] pwe;
  wire [15:0] O0, O1, O2, O3, O4, O5, O6, O7;

  assign Reg1ReadData = Re1sel4 ? O4 : 16'bz;  // Controlled_Buffer controlled_buffer_1
  assign Reg1ReadData = Re1sel5 ? O5 : 16'bz;  // Controlled_Buffer controlled_buffer_2
  assign Reg1ReadData = Re1sel6 ? O6 : 16'bz;  // Controlled_Buffer controlled_buffer_3
  assign Reg1ReadData = Re1sel7 ? O7 : 16'bz;  // Controlled_Buffer controlled_buffer_4
  Register16 register16_1 (.Out16Bits(O0), .we(we0), .clock(Clock), .reset(reset), .In16Bits({16{1'b0}}));
  Register16 register16_2 (.Out16Bits(O4), .we(we4), .clock(Clock), .reset(reset), .In16Bits(Data));
  assign Reg1ReadData = Re1sel0 ? O0 : 16'bz;  // Controlled_Buffer controlled_buffer_5
  assign Reg1ReadData = Re1sel1 ? O1 : 16'bz;  // Controlled_Buffer controlled_buffer_6
  assign Reg1ReadData = Re1sel2 ? O2 : 16'bz;  // Controlled_Buffer controlled_buffer_7
  assign Reg1ReadData = Re1sel3 ? O3 : 16'bz;  // Controlled_Buffer controlled_buffer_8
  // Probe on O0
  // Probe on O4
  Multiplexer #(.width(3), .enable("false")) multiplexer_1 (.in0(PickWE), .in1(3'b111), .out(pwe), .sel(jalWE));
  assign Reg2ReadData = Re2sel1 ? O1 : 16'bz;  // Controlled_Buffer controlled_buffer_9
  assign Reg2ReadData = Re2sel2 ? O2 : 16'bz;  // Controlled_Buffer controlled_buffer_10
  assign Reg2ReadData = Re2sel3 ? O3 : 16'bz;  // Controlled_Buffer controlled_buffer_11
  assign Reg2ReadData = Re2sel4 ? O4 : 16'bz;  // Controlled_Buffer controlled_buffer_12
  assign Reg2ReadData = Re2sel5 ? O5 : 16'bz;  // Controlled_Buffer controlled_buffer_13
  assign Reg2ReadData = Re2sel6 ? O6 : 16'bz;  // Controlled_Buffer controlled_buffer_14
  assign Reg2ReadData = Re2sel7 ? O7 : 16'bz;  // Controlled_Buffer controlled_buffer_15
  assign Reg2ReadData = Re2sel0 ? O0 : 16'bz;  // Controlled_Buffer controlled_buffer_16
  Decoder #(.select(3)) decoder_1 (
    .out0(Re1sel0), .out1(Re1sel1), .out2(Re1sel2), .out3(Re1sel3), .out4(Re1sel4), .out5(Re1sel5),
    .out6(Re1sel6), .out7(Re1sel7), .sel(Register1));  // open: en
  Decoder #(.select(3)) decoder_2 (
    .out0(we0), .out1(we1), .out2(we2), .out3(we3), .out4(we4), .out5(we5), .out6(we6), .out7(we7),
    .sel(pwe), .en(WE));
  // Probe on O1
  Register16 register16_3 (.Out16Bits(O1), .we(we1), .clock(Clock), .reset(reset), .In16Bits(Data));
  Register16 register16_4 (.Out16Bits(O5), .we(we5), .clock(Clock), .reset(reset), .In16Bits(Data));
  // Probe on O5
  Register16 register16_5 (.Out16Bits(O2), .we(we2), .clock(Clock), .reset(reset), .In16Bits(Data));
  Register16 register16_6 (.Out16Bits(O6), .we(we6), .clock(Clock), .reset(reset), .In16Bits(Data));
  // Probe on O2
  // Probe on O6
  Decoder #(.select(3)) decoder_3 (
    .out0(Re2sel0), .out1(Re2sel1), .out2(Re2sel2), .out3(Re2sel3), .out4(Re2sel4), .out5(Re2sel5),
    .out6(Re2sel6), .out7(Re2sel7), .sel(Register2));  // open: en
  // Probe on O3
  Register16 register16_7 (.Out16Bits(O3), .we(we3), .clock(Clock), .reset(reset), .In16Bits(Data));
  Register16 register16_8 (.Out16Bits(O7), .we(we7), .clock(Clock), .reset(reset), .In16Bits(Data));
  // Probe on O7

  // Other names for the same wires on the sheet: clk = Clock; d[15:0] = Data; jal = jalWE; Re1[2:0] = Register1;
  //   Re2[2:0] = Register2; ReadData1[15:0] = Reg1ReadData; ReadData2[15:0] = Reg2ReadData; rst = reset
endmodule

module ALU (
  input  [15:0] InputData1,
  input  [15:0] InputData2,
  input  [2:0] Shamt,
  input  [2:0] ALUop,
  output [15:0] OutputData,
  output equivalent,
  output GorE
);

  wire [15:0] add, LeftShift, NND, NOOR, RightShift, sub;

  SixteenBitAdder sixteenbitadder_1 (.result(add), .B(InputData2), .sub(1'b0), .A(InputData1));  // open: ovf
  SixteenBitAdder sixteenbitadder_2 (.result(sub), .B(InputData2), .sub(1'b1), .A(InputData1));  // open: ovf
  FullLeftShift fullleftshift_1 (.LSR(LeftShift), .ShiftAmount(Shamt), .DataToBeLS(InputData1));
  Equal equal_1 (.SubResult(sub), .eq(equivalent));
  GreaterOREqual greaterorequal_1 (.in_1(sub), .FirstGreater(GorE));
  assign NOOR = ~(InputData1 | InputData2);  // NOR_Gate nor_1, 16 bits wide
  assign NND = ~(InputData1 & InputData2);  // NAND_Gate nand_1, 16 bits wide
  FullRightShift fullrightshift_1 (.SRR(RightShift), .RSD(InputData1), .ShiftAmount(Shamt));
  Multiplexer #(.select(3), .width(16), .enable("false")) multiplexer_1 (
    .in0(add), .in1(add), .in2(sub), .in3(NOOR), .in4(NND), .in5(LeftShift), .in6(RightShift),
    .out(OutputData), .sel(ALUop));  // open: in7

  // Other names for the same wires on the sheet: I1[15:0] = InputData1; I2[15:0] = InputData2
endmodule

module OneBitAdder (
  input  a,
  input  b,
  input  Cin,
  output r,
  output Cout
);

  wire and_2_out, t1, xor_1_out;

  xor xor_1 (xor_1_out, a, b);
  and and_1 (t1, a, b);
  xor xor_2 (r, xor_1_out, Cin);
  and and_2 (and_2_out, Cin, xor_1_out);
  or or_1 (Cout, and_2_out, t1);
endmodule

module SixteenBitAdder (
  input  [15:0] A,
  input  sub,
  input  [15:0] B,
  output [15:0] result,
  output ovf
);

  wire onebitadder_1_cout, onebitadder_2_cout, onebitadder_3_cout, onebitadder_4_cout, onebitadder_5_cout,
       onebitadder_6_cout, onebitadder_7_cout, onebitadder_8_cout, onebitadder_9_cout, onebitadder_10_cout,
       onebitadder_11_cout, onebitadder_12_cout, onebitadder_13_cout, onebitadder_14_cout,
       onebitadder_15_cout, onebitadder_16_cout, xor_1_out, xor_2_out, xor_3_out, xor_4_out, xor_5_out,
       xor_6_out, xor_7_out, xor_8_out, xor_9_out, xor_10_out, xor_11_out, xor_12_out, xor_13_out,
       xor_14_out, xor_15_out, xor_16_out, xor_17_out;

  not not_1 (ovf, xor_1_out);
  xor xor_1 (xor_1_out, onebitadder_1_cout, onebitadder_2_cout);
  OneBitAdder onebitadder_1 (
    .a(A[15]), .b(xor_2_out), .Cin(onebitadder_2_cout), .r(result[15]), .Cout(onebitadder_1_cout));
  OneBitAdder onebitadder_2 (
    .a(A[14]), .b(xor_3_out), .Cin(onebitadder_3_cout), .r(result[14]), .Cout(onebitadder_2_cout));
  OneBitAdder onebitadder_3 (
    .a(A[13]), .b(xor_4_out), .Cin(onebitadder_4_cout), .r(result[13]), .Cout(onebitadder_3_cout));
  OneBitAdder onebitadder_4 (
    .a(A[12]), .b(xor_5_out), .Cin(onebitadder_5_cout), .r(result[12]), .Cout(onebitadder_4_cout));
  OneBitAdder onebitadder_5 (
    .a(A[11]), .b(xor_6_out), .Cin(onebitadder_6_cout), .r(result[11]), .Cout(onebitadder_5_cout));
  OneBitAdder onebitadder_6 (
    .a(A[10]), .b(xor_7_out), .Cin(onebitadder_7_cout), .r(result[10]), .Cout(onebitadder_6_cout));
  xor xor_2 (xor_2_out, sub, B[15]);
  OneBitAdder onebitadder_7 (
    .a(A[9]), .b(xor_8_out), .Cin(onebitadder_8_cout), .r(result[9]), .Cout(onebitadder_7_cout));
  xor xor_3 (xor_3_out, sub, B[14]);
  OneBitAdder onebitadder_8 (
    .a(A[8]), .b(xor_9_out), .Cin(onebitadder_9_cout), .r(result[8]), .Cout(onebitadder_8_cout));
  xor xor_4 (xor_4_out, sub, B[13]);
  OneBitAdder onebitadder_9 (
    .a(A[7]), .b(xor_10_out), .Cin(onebitadder_10_cout), .r(result[7]), .Cout(onebitadder_9_cout));
  xor xor_5 (xor_5_out, sub, B[12]);
  OneBitAdder onebitadder_10 (
    .a(A[6]), .b(xor_11_out), .Cin(onebitadder_11_cout), .r(result[6]), .Cout(onebitadder_10_cout));
  OneBitAdder onebitadder_11 (
    .a(A[5]), .b(xor_12_out), .Cin(onebitadder_12_cout), .r(result[5]), .Cout(onebitadder_11_cout));
  xor xor_6 (xor_6_out, sub, B[11]);
  OneBitAdder onebitadder_12 (
    .a(A[4]), .b(xor_13_out), .Cin(onebitadder_13_cout), .r(result[4]), .Cout(onebitadder_12_cout));
  OneBitAdder onebitadder_13 (
    .a(A[3]), .b(xor_14_out), .Cin(onebitadder_14_cout), .r(result[3]), .Cout(onebitadder_13_cout));
  OneBitAdder onebitadder_14 (
    .a(A[2]), .b(xor_16_out), .Cin(onebitadder_15_cout), .r(result[2]), .Cout(onebitadder_14_cout));
  xor xor_7 (xor_7_out, sub, B[10]);
  xor xor_8 (xor_8_out, sub, B[9]);
  OneBitAdder onebitadder_15 (
    .a(A[1]), .b(xor_15_out), .Cin(onebitadder_16_cout), .r(result[1]), .Cout(onebitadder_15_cout));
  xor xor_9 (xor_9_out, sub, B[8]);
  xor xor_10 (xor_10_out, sub, B[7]);
  xor xor_11 (xor_11_out, sub, B[6]);
  OneBitAdder onebitadder_16 (.a(A[0]), .b(xor_17_out), .Cin(sub), .r(result[0]), .Cout(onebitadder_16_cout));
  xor xor_12 (xor_12_out, sub, B[5]);
  xor xor_13 (xor_13_out, sub, B[4]);
  xor xor_14 (xor_14_out, sub, B[3]);
  xor xor_15 (xor_15_out, sub, B[1]);
  xor xor_16 (xor_16_out, sub, B[2]);
  xor xor_17 (xor_17_out, sub, B[0]);

  // Other names for the same wires on the sheet: i6 = A[6]; i7 = A[7]; i8 = A[8]; i10 = A[10]; i12 = A[12];
  //   i14 = A[14]; i15 = A[15]
endmodule

module OneLeftShift (
  input  ifShift,
  input  [15:0] OneSB,
  output [15:0] OneSR
);

  Multiplexer #(.width(16), .enable("false")) multiplexer_1 (
    .in0(OneSB), .in1({OneSB[14:0], 1'b0}), .out(OneSR), .sel(ifShift));
endmodule

module TwoLeftShift (
  input  ifShift2,
  input  [15:0] TwoSB,
  output [15:0] TwoSR
);

  Multiplexer #(.width(16), .enable("false")) multiplexer_1 (
    .in0(TwoSB), .in1({TwoSB[13:0], 2'b00}), .out(TwoSR), .sel(ifShift2));
endmodule

module FourShiftBit (
  input  ifShift4,
  input  [15:0] FourSB,
  output [15:0] FourSR
);

  Multiplexer #(.width(16), .enable("false")) multiplexer_1 (
    .in0(FourSB), .in1({FourSB[11:0], 4'b0000}), .out(FourSR), .sel(ifShift4));
endmodule

module FullLeftShift (
  input  [15:0] DataToBeLS,
  input  [2:0] ShiftAmount,
  output [15:0] LSR
);

  wire [15:0] fourshiftbit_1_foursr, twoleftshift_1_twosr;

  FourShiftBit fourshiftbit_1 (.FourSR(fourshiftbit_1_foursr), .ifShift4(ShiftAmount[2]), .FourSB(DataToBeLS));
  TwoLeftShift twoleftshift_1 (.TwoSR(twoleftshift_1_twosr), .TwoSB(fourshiftbit_1_foursr), .ifShift2(ShiftAmount[1]));
  OneLeftShift oneleftshift_1 (.OneSR(LSR), .OneSB(twoleftshift_1_twosr), .ifShift(ShiftAmount[0]));
endmodule

module OneRightShift (
  input  ifShift,
  input  [15:0] OneSRD,
  output [15:0] OSRD
);

  Multiplexer #(.width(16), .enable("false")) multiplexer_1 (
    .in0(OneSRD), .in1({1'b0, OneSRD[15:1]}), .out(OSRD), .sel(ifShift));
endmodule

module TwoRightShift (
  input  ifShiftTwo,
  input  [15:0] TwoSRD,
  output [15:0] TwoSR
);

  Multiplexer #(.width(16), .enable("false")) multiplexer_1 (
    .in0(TwoSRD), .in1({2'b00, TwoSRD[15:2]}), .out(TwoSR), .sel(ifShiftTwo));
endmodule

module FourRightShift (
  input  ifShiftFour,
  input  [15:0] FourSRD,
  output [15:0] FourSR
);

  Multiplexer #(.width(16), .enable("false")) multiplexer_1 (
    .in0(FourSRD), .in1({4'b0000, FourSRD[15:4]}), .out(FourSR), .sel(ifShiftFour));
endmodule

module FullRightShift (
  input  [15:0] RSD,
  input  [2:0] ShiftAmount,
  output [15:0] SRR
);

  wire [15:0] onerightshift_1_osrd, tworightshift_1_twosr;

  OneRightShift onerightshift_1 (.ifShift(ShiftAmount[0]), .OneSRD(RSD), .OSRD(onerightshift_1_osrd));
  TwoRightShift tworightshift_1 (
    .ifShiftTwo(ShiftAmount[1]), .TwoSRD(onerightshift_1_osrd), .TwoSR(tworightshift_1_twosr));
  FourRightShift fourrightshift_1 (.ifShiftFour(ShiftAmount[2]), .FourSRD(tworightshift_1_twosr), .FourSR(SRR));
endmodule

module Equal (
  input  [15:0] SubResult,
  output eq
);

  wire nand_1_out, xor_1_out, xor_2_out, xor_3_out, xor_4_out, xor_5_out, xor_6_out, xor_7_out, xor_8_out,
       xor_9_out, xor_10_out, xor_11_out, xor_12_out, xor_13_out, xor_14_out, xor_15_out, xor_16_out;

  xor xor_1 (xor_1_out, 1'b1, SubResult[0]);
  xor xor_2 (xor_2_out, 1'b1, SubResult[1]);
  xor xor_3 (xor_3_out, 1'b1, SubResult[2]);
  xor xor_4 (xor_4_out, 1'b1, SubResult[3]);
  xor xor_5 (xor_5_out, 1'b1, SubResult[4]);
  xor xor_6 (xor_6_out, 1'b1, SubResult[5]);
  xor xor_7 (xor_7_out, 1'b1, SubResult[6]);
  xor xor_8 (xor_8_out, 1'b1, SubResult[7]);
  not not_1 (eq, nand_1_out);
  nand nand_1 (nand_1_out, xor_1_out, xor_2_out, xor_3_out, xor_4_out, xor_5_out, xor_6_out, xor_7_out, xor_8_out, xor_9_out, xor_10_out, xor_11_out, xor_12_out, xor_13_out, xor_14_out, xor_15_out, xor_16_out);
  xor xor_9 (xor_9_out, 1'b1, SubResult[8]);
  xor xor_10 (xor_10_out, 1'b1, SubResult[9]);
  xor xor_11 (xor_11_out, 1'b1, SubResult[10]);
  xor xor_12 (xor_12_out, 1'b1, SubResult[11]);
  xor xor_13 (xor_13_out, 1'b1, SubResult[12]);
  xor xor_14 (xor_14_out, 1'b1, SubResult[13]);
  xor xor_15 (xor_15_out, 1'b1, SubResult[14]);
  xor xor_16 (xor_16_out, 1'b1, SubResult[15]);
endmodule

module GreaterOREqual (
  input  [15:0] in_1,
  output FirstGreater
);

  wire and_1_out, xor_1_out, xor_2_out, xor_3_out, xor_4_out, xor_5_out, xor_6_out, xor_7_out, xor_8_out,
       xor_9_out, xor_10_out, xor_11_out, xor_12_out, xor_13_out, xor_14_out, xor_15_out, xor_16_out,
       xor_17_out;

  xor xor_1 (xor_1_out, 1'b1, in_1[0]);
  xor xor_2 (xor_2_out, 1'b1, in_1[1]);
  xor xor_3 (xor_3_out, 1'b1, in_1[2]);
  xor xor_4 (xor_4_out, 1'b1, in_1[3]);
  xor xor_5 (xor_5_out, 1'b1, in_1[4]);
  xor xor_6 (xor_6_out, 1'b1, in_1[5]);
  xor xor_7 (xor_7_out, 1'b1, in_1[6]);
  xor xor_8 (xor_8_out, 1'b1, in_1[7]);
  and and_1 (and_1_out, xor_1_out, xor_2_out, xor_3_out, xor_4_out, xor_5_out, xor_6_out, xor_7_out, xor_8_out, xor_9_out, xor_10_out, xor_11_out, xor_12_out, xor_13_out, xor_15_out, xor_16_out, xor_17_out);
  xor xor_9 (xor_9_out, 1'b1, in_1[8]);
  or or_1 (FirstGreater, and_1_out, xor_14_out);
  xor xor_10 (xor_10_out, 1'b1, in_1[9]);
  xor xor_11 (xor_11_out, 1'b1, in_1[10]);
  xor xor_12 (xor_12_out, 1'b1, in_1[11]);
  xor xor_13 (xor_13_out, 1'b1, in_1[12]);
  xor xor_14 (xor_14_out, in_1[15], 1'b1);
  xor xor_15 (xor_15_out, 1'b1, in_1[13]);
  xor xor_16 (xor_16_out, 1'b1, in_1[14]);
  xor xor_17 (xor_17_out, 1'b1, in_1[15]);

  // Other names for the same wires on the sheet: SubResult[15:0] = in_1
endmodule

module InstructionSplitter (
  input  [15:0] Ins,
  output [11:0] adrs,
  output [3:0] opcode,
  output [2:0] rs,
  output [5:0] Immed,
  output [2:0] rt,
  output [2:0] shamt,
  output [2:0] rd
);


  assign adrs = Ins[11:0];
  assign Immed = Ins[5:0];
  assign opcode = Ins[15:12];
  assign rd = Ins[5:3];
  assign rs = Ins[11:9];
  assign rt = Ins[8:6];
  assign shamt = Ins[2:0];

  // Notes on the sheet:
  //   R-type
  //   I-type
  //   J-type
endmodule

module OpCrl (
  input  [3:0] OpCode,
  output [2:0] ALUop,
  output RWE,
  output jalWE,
  output AddImm,
  output RAMwe,
  output RWD,
  output RDwe,
  output [1:0] PCop,
  output InputWE,
  output TTY,
  output [1:0] b
);

  wire add, addi, j, jr, nnd, noor, sl, sr, sub;

  Decoder #(.select(4)) decoder_1 (
    .out0(add), .out1(addi), .out2(sub), .out3(noor), .out4(nnd), .out5(sl), .out6(sr), .out7(RWD),
    .out8(RAMwe), .out9(b[0]), .out10(b[1]), .out11(j), .out12(jr), .out13(jalWE), .out14(InputWE),
    .out15(TTY), .sel(OpCode));  // open: en
  or or_1 (AddImm, addi, RAMwe, RWD);
  nor nor_1 (RDwe, RWD, addi, InputWE);
  or or_2 (ALUop[0], noor, add, addi, RAMwe, RWD, sl);
  or or_3 (ALUop[1], sub, noor, sr);
  or or_4 (ALUop[2], nnd, sl, sr);
  or or_5 (RWE, add, addi, sub, noor, nnd, sl, sr, RWD, jalWE, InputWE);
  or or_6 (PCop[0], b[1], b[0], jr);
  or or_7 (PCop[1], j, jr, jalWE);

  // Other names for the same wires on the sheet: beq = b[0]; bge = b[1]; inn = InputWE; jal = jalWE; lw = RWD;
  //   owt = TTY; sw = RAMwe
endmodule

module PC (
  input  [15:0] in_1,
  input  clk,
  input  rst,
  output [15:0] out_4
);

  wire not_1_out;

  not not_1 (not_1_out, clk);
  Register16 register16_1 (.Out16Bits(out_4), .we(1'b1), .clock(not_1_out), .reset(rst), .In16Bits(in_1));
endmodule

module memory_latch (
  input  [15:0] address,
  input  WE,
  input  clk,
  input  [15:0] data_in,
  output [15:0] address_latched,
  output WE_latched,
  output OE_latched,
  output [15:0] data_in_latched
);

  wire clk_t, DMwe_latch_q;
  wire [15:0] addr_latch_q;

  not not_1 (clk_t, clk);
  Register #(.width(16), .trigger("falling")) addr_latch (
    .D(address), .en(WE), .clk(clk_t), .Q(addr_latch_q));  // open: clr
  D_Flip_Flop #(.trigger("falling")) DMwe_latch (.D(WE), .clk(clk_t), .Q(DMwe_latch_q));  // open: Qn, preset, reset
  Register #(.width(16), .trigger("falling")) data_to_be_written (
    .D(data_in), .en(WE), .clk(clk_t), .Q(data_in_latched));  // open: clr
  Multiplexer #(.width(16), .enable("false")) multiplexer_1 (
    .in0(address), .in1(addr_latch_q), .out(address_latched), .sel(DMwe_latch_q));
  and and_1 (WE_latched, clk_t, DMwe_latch_q);
  not not_2 (OE_latched, WE_latched);
endmodule

module PCNav (
  input  [15:0] PC,
  input  [15:0] Imm,
  input  b,
  input  [1:0] PCop,
  input  [15:0] rs,
  input  [11:0] addr,
  output [15:0] norm,
  output [15:0] nxt
);

  wire [15:0] addr_t, br, jAddr, sixteenbitadder_3_result;

  SixteenBitAdder sixteenbitadder_1 (.result(norm), .B(16'h1), .A(PC));  // open: ovf, sub
  SixteenBitAdder sixteenbitadder_2 (.result(jAddr), .A(PC));  // open: ovf, B, sub
  assign addr_t = {{4{1'b0}}, addr};  // Bit_Extender bit_extender_1
  SixteenBitAdder sixteenbitadder_3 (.result(sixteenbitadder_3_result), .B(Imm), .A(norm));  // open: ovf, sub
  Multiplexer #(.width(16), .enable("false")) multiplexer_1 (
    .in0(norm), .in1(sixteenbitadder_3_result), .out(br), .sel(b));
  Multiplexer #(.select(2), .width(16), .enable("false")) multiplexer_2 (
    .in0(norm), .in1(br), .in2(addr_t), .in3(rs), .out(nxt), .sel(PCop));

  // Other names for the same wires on the sheet: op[1:0] = PCop
endmodule
