// Logisim project ignition.circ as structural Verilog: 1 circuit, main circuit main
module main (
  input  start_engine,
  input  engine_running,
  output starter_motor,
  output ignition_coil
);

  wire and_1_out, and_2_out, and_3_out, and_4_out, and_5_out, and_6_out, and_7_out, and_8_out, clk, D0, D1,
       not_1_out, not_2_out, not_3_out, not_4_out, not_5_out, not_6_out, not_7_out, or_1_out, or_2_out,
       or_3_out, Q0, Q1;

  not not_1 (not_1_out, Q0);
  Clock clock_1 (.out(clk));
  not not_2 (not_2_out, start_engine);
  and and_1 (and_1_out, Q1, start_engine);
  or or_1 (or_1_out, not_1_out, engine_running, Q1);
  not not_3 (not_3_out, Q0);
  not not_4 (not_4_out, engine_running);
  not not_5 (not_5_out, Q0);
  and and_2 (and_2_out, Q0, engine_running);
  and and_3 (and_3_out, not_3_out, not_4_out);
  or or_2 (or_2_out, and_1_out, engine_running);
  and and_4 (and_4_out, start_engine, or_1_out);
  or or_3 (or_3_out, and_2_out, and_3_out);
  and and_5 (and_5_out, not_5_out, Q1, not_2_out, engine_running);
  and and_6 (and_6_out, Q1, or_3_out);
  and and_7 (and_7_out, Q0, or_2_out);
  not not_6 (not_6_out, Q0);
  not not_7 (not_7_out, Q1);
  D_Flip_Flop u_Q0 (.D(D0), .clk(clk), .Q(Q0));  // open: Qn, preset, reset
  D_Flip_Flop u_Q1 (.D(D1), .clk(clk), .Q(Q1));  // open: Qn, preset, reset
  and and_8 (and_8_out, Q0, not_7_out);
  or or_4 (D0, and_5_out, and_7_out);
  or or_5 (D1, and_4_out, and_6_out);
  and and_9 (starter_motor, not_6_out, Q1);
  or or_6 (ignition_coil, starter_motor, and_8_out);

  // Other names for the same wires on the sheet: I1 = start_engine; I2 = engine_running; IC = ignition_coil;
  //   SM = starter_motor
endmodule
