// Logisim project my_adder.circ as structural Verilog: 2 circuits, main circuit Bit16Adder
module Bit16Adder (
  input  [15:0] A,
  input  sub,
  input  [15:0] B,
  output [15:0] result,
  output ovf
);

  wire ad1_1_cout, ad1_2_cout, ad1_3_cout, ad1_4_cout, ad1_5_cout, ad1_6_cout, ad1_7_cout, ad1_8_cout,
       ad1_9_cout, ad1_10_cout, ad1_11_cout, ad1_12_cout, ad1_13_cout, ad1_14_cout, ad1_15_cout, ad1_16_cout,
       xor_1_out, xor_2_out, xor_3_out, xor_4_out, xor_5_out, xor_6_out, xor_7_out, xor_8_out, xor_9_out,
       xor_10_out, xor_11_out, xor_12_out, xor_13_out, xor_14_out, xor_15_out, xor_16_out, xor_17_out;

  not not_1 (ovf, xor_1_out);
  xor xor_1 (xor_1_out, result[15], ad1_2_cout);
  ad1 ad1_1 (.a(A[15]), .b(xor_2_out), .Cin(ad1_2_cout), .r(result[15]), .Cout(ad1_1_cout));
  ad1 ad1_2 (.a(A[14]), .b(xor_3_out), .Cin(ad1_3_cout), .r(result[14]), .Cout(ad1_2_cout));
  ad1 ad1_3 (.a(A[13]), .b(xor_4_out), .Cin(ad1_4_cout), .r(result[13]), .Cout(ad1_3_cout));
  ad1 ad1_4 (.a(A[12]), .b(xor_5_out), .Cin(ad1_5_cout), .r(result[12]), .Cout(ad1_4_cout));
  ad1 ad1_5 (.a(A[11]), .b(xor_6_out), .Cin(ad1_6_cout), .r(result[11]), .Cout(ad1_5_cout));
  ad1 ad1_6 (.a(A[10]), .b(xor_7_out), .Cin(ad1_7_cout), .r(result[10]), .Cout(ad1_6_cout));
  xor xor_2 (xor_2_out, sub, B[15]);
  ad1 ad1_7 (.a(A[9]), .b(xor_8_out), .Cin(ad1_8_cout), .r(result[9]), .Cout(ad1_7_cout));
  xor xor_3 (xor_3_out, sub, B[14]);
  ad1 ad1_8 (.a(A[8]), .b(xor_9_out), .Cin(ad1_9_cout), .r(result[8]), .Cout(ad1_8_cout));
  xor xor_4 (xor_4_out, sub, B[13]);
  ad1 ad1_9 (.a(A[7]), .b(xor_10_out), .Cin(ad1_10_cout), .r(result[7]), .Cout(ad1_9_cout));
  xor xor_5 (xor_5_out, sub, B[12]);
  ad1 ad1_10 (.a(A[6]), .b(xor_11_out), .Cin(ad1_11_cout), .r(result[6]), .Cout(ad1_10_cout));
  ad1 ad1_11 (.a(A[5]), .b(xor_12_out), .Cin(ad1_12_cout), .r(result[5]), .Cout(ad1_11_cout));
  xor xor_6 (xor_6_out, sub, B[11]);
  ad1 ad1_12 (.a(A[4]), .b(xor_14_out), .Cin(ad1_13_cout), .r(result[4]), .Cout(ad1_12_cout));
  ad1 ad1_13 (.a(A[3]), .b(xor_13_out), .Cin(ad1_14_cout), .r(result[3]), .Cout(ad1_13_cout));
  ad1 ad1_14 (.a(A[2]), .b(xor_16_out), .Cin(ad1_15_cout), .r(result[2]), .Cout(ad1_14_cout));
  xor xor_7 (xor_7_out, sub, B[10]);
  xor xor_8 (xor_8_out, sub, B[9]);
  ad1 ad1_15 (.a(A[1]), .b(xor_15_out), .Cin(ad1_16_cout), .r(result[1]), .Cout(ad1_15_cout));
  xor xor_9 (xor_9_out, sub, B[8]);
  xor xor_10 (xor_10_out, sub, B[7]);
  xor xor_11 (xor_11_out, sub, B[6]);
  ad1 ad1_16 (.a(A[0]), .b(xor_17_out), .Cin(sub), .r(result[0]), .Cout(ad1_16_cout));
  xor xor_12 (xor_12_out, sub, B[5]);
  xor xor_13 (xor_13_out, sub, B[3]);
  xor xor_14 (xor_14_out, sub, B[4]);
  xor xor_15 (xor_15_out, sub, B[1]);
  xor xor_16 (xor_16_out, sub, B[2]);
  xor xor_17 (xor_17_out, sub, B[0]);

  // Other names for the same wires on the sheet: i6 = A[6]; i7 = A[7]; i8 = A[8]; i10 = A[10]; i12 = A[12];
  //   i14 = A[14]; i15 = A[15]
endmodule

module ad1 (
  input  a,
  input  b,
  input  Cin,
  output r,
  output Cout
);

  wire and_2_out, t1, xor_1_out;

  xor xor_1 (xor_1_out, a, b);
  and and_1 (t1, a, b);
  xor xor_2 (r, xor_1_out, Cin);
  and and_2 (and_2_out, Cin, xor_1_out);
  or or_1 (Cout, and_2_out, t1);
endmodule
